// Logisim project hi.circ as structural Verilog
module Warmup (
  input  in_1
);

  wire clock_1_out, d_ff_1_q;

  Clock #(.highDuration(3), .lowDuration(3), .phaseOffset(1)) clock_1 (.out(clock_1_out));
  D_Flip_Flop #(.trigger("high")) d_ff_1 (.D(in_1), .clk(clock_1_out), .Q(d_ff_1_q));  // open: Qn, preset, reset
  LED led_1 (.in(d_ff_1_q));
endmodule

module FA (
  input  B,
  input  A,
  input  Cin,
  output S,
  output Cout
);

  wire and_1_out, and_2_out, xor_1_out;

  xor xor_1 (xor_1_out, A, B);
  and and_1 (and_1_out, A, B);
  xor xor_2 (S, xor_1_out, Cin);
  and and_2 (and_2_out, Cin, xor_1_out);
  or or_1 (Cout, and_1_out, and_2_out);
endmodule

module ADDSUB4 (
  input  Sub,
  input  [3:0] B,
  input  [3:0] A,
  output [3:0] S,
  output C3,
  output C2,
  output C1,
  output Z,
  output N,
  output C,
  output V
);

  wire xor_1_out, xor_2_out, xor_3_out, xor_4_out, xor_5_out, xor_6_out;

  xor xor_1 (xor_1_out, Sub, B[0]);
  xor xor_2 (xor_2_out, Sub, B[1]);
  xor xor_3 (xor_3_out, Sub, B[2]);
  xor xor_4 (xor_4_out, Sub, B[3]);
  FA fa_1 (.B(xor_1_out), .A(A[0]), .Cin(Sub), .S(S[0]), .Cout(C1));
  FA fa_2 (.B(xor_2_out), .A(A[1]), .Cin(C1), .S(S[1]), .Cout(C2));
  FA fa_3 (.B(xor_3_out), .A(A[2]), .Cin(C2), .S(S[2]), .Cout(C3));
  xor xor_5 (xor_5_out, N, B[3]);
  and and_1 (V, xor_5_out, xor_6_out);
  xor xor_6 (xor_6_out, N, A[3]);
  FA fa_4 (.B(xor_4_out), .A(A[3]), .Cin(C3), .S(N), .Cout(C));
  nor nor_1 (Z, S[0], S[1], S[2], N);

  assign S[3] = N;
endmodule
